# Fritzing sketch schema (saved by Fritzing 0.9.5d)

parts:
  Mod1 = Raspberry Pi Pico
  LCD1 = elegoo-2.8in-tft-display
  UP = Pushbutton [package="[THT]"]
  RIGHT = Pushbutton [package="[THT]"]
  LEFT = Pushbutton [package="[THT]"]
  DOWN = Pushbutton [package="[THT]"]
  A = Pushbutton [package="[THT]"]
  B = Pushbutton [package="[THT]"]
  SKU1 = Module HP SKU00060

nets:
  N1: Mod1.pin_1, UP.Pin_3
  N2: Mod1.pin_2, DOWN.Pin_3, DOWN.Pin_4
  N3: Mod1.pin_4, RIGHT.Pin_3, RIGHT.Pin_4
  N4: Mod1.pin_5, LEFT.Pin_3
  N5: Mod1.pin_6, B.Pin_3
  N6: Mod1.pin_7, A.Pin_3
  N7: Mod1.pin_8, Mod1.pin_33, Mod1.pin_38, LCD1.GND, UP.Pin_1, UP.Pin_2, RIGHT.Pin_1, LEFT.Pin_1, LEFT.Pin_2, DOWN.Pin_1, DOWN.Pin_2, A.Pin_1, A.Pin_2, B.Pin_1, B.Pin_2
  N8: Mod1.pin_11, LCD1.LCD_D2
  N9: Mod1.pin_12, LCD1.LCD_D3
  N10: Mod1.pin_14, LCD1.LCD_D4
  N11: Mod1.pin_15, LCD1.LCD_D5
  N12: Mod1.pin_16, LCD1.LCD_D6
  N13: Mod1.pin_17, LCD1.LCD_D7
  N14: Mod1.pin_19, LCD1.LCD_D0
  N15: Mod1.pin_20, LCD1.LCD_D1
  N16: Mod1.pin_21, LCD1.LCD_RD
  N17: Mod1.pin_22, LCD1.LCD_WR
  N18: Mod1.pin_24, LCD1.LCD_RS
  N19: Mod1.pin_25, LCD1.LCD_CS
  N20: Mod1.pin_26, LCD1.LCD_RST
  N21: Mod1.pin_34, SKU1.In
  N22: Mod1.pin_36, LCD1.+3.3V

custom parts:
  Raspberry Pi Pico: Raspberry Pi Pico. Based around the RP2040 microcontroller the Pico is a low cost microcontroller device bringing Raspberry Pi quality, cost, and easy of use to the microcontroller space. Jan 2021, Split part in to two versions: tht (this one) and SMD. This one will drill holes for a .1 in header in pcb to allow plugging in the module as well as providing pads to solder the module to the top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
  elegoo-2.8in-tft-display: 2.8 Inch TFT LCD Touch Screen with SD Card Socket. 240*320 pixels RGB. 4 chip white LED backlight.
